# Fritzing sketch 19CCE384_Circuit_Diagram (saved by Fritzing 0.9.3b)
circuit board: 8.46667cm x 5.64444cm
breadboards: 1

parts:
  Part1 = Arduino Motor Shield (Rev3)
  IC1 = L293D [package=THT]
  BAT1 = BC9VPC [package=bc9vpc]
  M1 = DC Motor
  M2 = DC Motor
  IC2 = L293D [package=THT]
  M3 = DC Motor
  M4 = DC Motor
  BAT2 = BC9VPC [package=bc9vpc]
  J1 = Basic Servo
  HC-SR04_Sensor_1 = HC-SR04 Ultrasonic Distance Sensor
  M5 = DC Motor
  Part2 = Bluetooth HC-05 Macho
  S1 = SWITCH-MOMENTARY-2 [package=tactile_switch_smd-2]
  S2 = SWITCH-MOMENTARY-2 [package=tactile_switch_smd-2]
  IC3 = Voltage Regulator [package=78xxl]

nets:
  VCC: Part1.5V, J1.vcc, HC-SR04_Sensor_1.VCC, Part2.VCC
  GND: Part1.GND, J1.gnd, HC-SR04_Sensor_1.ECHO, M5.pin_2, Part2.GND, S2.1
  N1: Part1.D8/BreakeB, IC1.In_3
  N2: Part1.D9/BreakeA, IC2.In_1
  N3: Part1.D10_PWM, IC2.In_2
  N4: Part1.D11_PWM/B, J1.pulse
  N5: Part1.D12/DirA, IC2.In_4
  N6: Part1.D13/DirB, IC2.In_3
  N7: Part1.IOREF, Part2.RXD
  N8: Part1.D2, IC1.In_1
  N9: Part1.D3_PWM/A, IC1.In_2
  N10: Part1.D4, M5.pin_1
  N11: Part1.D5_PWM, HC-SR04_Sensor_1.TRIG
  N12: Part1.D6_PWM, HC-SR04_Sensor_1.GND
  N13: Part1.D7, IC1.In_4
  N14: Part1.VIN, BAT2.V+
  N15: IC1.Enable_1, IC1.+Vmotor, IC1.Enable_2, IC1.+V, IC2.Enable_1, IC2.+Vmotor, IC2.Enable_2, IC2.+V, IC3.OUT
  N16: IC1.Out_1_(_Controlled_by_Enable_1_), M1.pin_1
  N17: IC1.0V, BAT1.V-, IC2.0V, IC3.GND
  N18: IC1.Out_2_(_Controlled_by_Enable_1_), M1.pin_2
  N19: IC1.Out_3_(_Controlled_by_Enable_2_), M2.pin_2
  N20: IC1.Out_4_(_Controlled_by_Enable_2_), M2.pin_1
  N21: BAT1.V+, S1.2
  N22: IC2.Out_1_(_Controlled_by_Enable_1_), M3.pin_1
  N23: IC2.Out_2_(_Controlled_by_Enable_1_), M3.pin_2
  N24: IC2.Out_3_(_Controlled_by_Enable_2_), M4.pin_2
  N25: IC2.Out_4_(_Controlled_by_Enable_2_), M4.pin_1
  N26: BAT2.V-, S2.2
  N27: S1.1, IC3.IN
